// Logisim project hammingCode.circ as structural Verilog: 2 circuits, main circuit main
module main (
  input  A,
  input  B,
  input  C,
  input  D,
  input  [2:0] in_5,
  output out_6,
  output out_7,
  output out_8,
  output out_9
);

  wire decoder_1_out0, decoder_1_out1, decoder_1_out2, decoder_1_out3, decoder_1_out4, decoder_1_out5,
       decoder_1_out6, decoder_1_out7, multiplexer_1_out, multiplexer_2_out, multiplexer_4_out,
       n3_8_decoder_1_out_4, n3_8_decoder_1_out_5, n3_8_decoder_1_out_6, n3_8_decoder_1_out_7,
       n3_8_decoder_1_out_8, n3_8_decoder_1_out_9, n3_8_decoder_1_out_10, n3_8_decoder_1_out_11, not_1_out,
       not_2_out, not_3_out, not_4_out, not_5_out, not_6_out, not_7_out, xor_1_out, xor_2_out, xor_3_out,
       xor_4_out, xor_5_out, xor_6_out, xor_7_out, xor_8_out, xor_9_out, xor_10_out, xor_11_out, xor_12_out,
       xor_13_out;

  xor xor_1 (xor_1_out, A, B, D);
  xor xor_2 (xor_2_out, A, C, D);
  xor xor_3 (xor_3_out, B, C, D);
  LED led_1 (.in(xor_1_out));
  LED led_2 (.in(xor_2_out));
  LED led_3 (.in(A));
  LED led_4 (.in(xor_3_out));
  LED led_5 (.in(B));
  LED led_6 (.in(C));
  LED led_7 (.in(D));
  Decoder #(.select(3), .enable("false")) decoder_1 (
    .out0(decoder_1_out0), .out1(decoder_1_out1), .out2(decoder_1_out2), .out3(decoder_1_out3),
    .out4(decoder_1_out4), .out5(decoder_1_out5), .out6(decoder_1_out6), .out7(decoder_1_out7), .sel(in_5));
  xor xor_4 (xor_4_out, xor_1_out, decoder_1_out0);
  xor xor_5 (xor_5_out, xor_2_out, decoder_1_out1);
  xor xor_6 (xor_6_out, A, decoder_1_out2);
  xor xor_7 (xor_7_out, xor_3_out, decoder_1_out3);
  xor xor_8 (xor_8_out, B, decoder_1_out4);
  xor xor_9 (xor_9_out, C, decoder_1_out5);
  xor xor_10 (xor_10_out, D, decoder_1_out6);
  LED led_8 (.in(xor_4_out));
  LED led_9 (.in(xor_5_out));
  LED led_10 (.in(xor_6_out));
  LED led_11 (.in(xor_7_out));
  LED led_12 (.in(xor_8_out));
  LED led_13 (.in(xor_9_out));
  LED led_14 (.in(xor_10_out));
  xor xor_11 (xor_11_out, xor_4_out, xor_6_out, xor_8_out, xor_10_out);
  xor xor_12 (xor_12_out, xor_6_out, xor_5_out, xor_9_out, xor_10_out);
  xor xor_13 (xor_13_out, xor_7_out, xor_8_out, xor_9_out, xor_10_out);
  _3_8_decoder u_3_8_decoder_1 (
    .in_1(xor_13_out), .in_2(xor_12_out), .in_3(xor_11_out), .out_4(n3_8_decoder_1_out_4),
    .out_5(n3_8_decoder_1_out_5), .out_6(n3_8_decoder_1_out_6), .out_7(n3_8_decoder_1_out_7),
    .out_8(n3_8_decoder_1_out_8), .out_9(n3_8_decoder_1_out_9), .out_10(n3_8_decoder_1_out_10),
    .out_11(n3_8_decoder_1_out_11));
  not not_1 (not_1_out, xor_6_out);
  not not_2 (not_2_out, xor_8_out);
  not not_3 (not_3_out, xor_4_out);
  not not_4 (not_4_out, xor_5_out);
  not not_5 (not_5_out, xor_7_out);
  not not_6 (not_6_out, xor_9_out);
  not not_7 (not_7_out, xor_10_out);
  Multiplexer #(.enable("false")) multiplexer_1 (
    .in0(xor_4_out), .in1(not_3_out), .out(multiplexer_1_out), .sel(n3_8_decoder_1_out_5));
  Multiplexer #(.enable("false")) multiplexer_2 (
    .in0(xor_5_out), .in1(not_4_out), .out(multiplexer_2_out), .sel(n3_8_decoder_1_out_6));
  Multiplexer #(.enable("false")) multiplexer_3 (
    .in0(xor_6_out), .in1(not_1_out), .out(out_6), .sel(n3_8_decoder_1_out_7));
  Multiplexer #(.enable("false")) multiplexer_4 (
    .in0(xor_7_out), .in1(not_5_out), .out(multiplexer_4_out), .sel(n3_8_decoder_1_out_8));
  Multiplexer #(.enable("false")) multiplexer_5 (
    .in0(xor_8_out), .in1(not_2_out), .out(out_7), .sel(n3_8_decoder_1_out_9));
  Multiplexer #(.enable("false")) multiplexer_6 (
    .in0(xor_9_out), .in1(not_6_out), .out(out_8), .sel(n3_8_decoder_1_out_10));
  Multiplexer #(.enable("false")) multiplexer_7 (
    .in0(xor_10_out), .in1(not_7_out), .out(out_9), .sel(n3_8_decoder_1_out_11));
  LED led_15 (.in(multiplexer_1_out));
  LED led_16 (.in(multiplexer_2_out));
  LED led_17 (.in(out_6));
  LED led_18 (.in(multiplexer_4_out));
  LED led_19 (.in(out_7));
  LED led_20 (.in(out_8));
  LED led_21 (.in(out_9));
  Hex_Digit_Display hex_digit_display_1 (.value({out_6, out_7, out_8, out_9}));  // open: dp

  // Notes on the sheet:
  //   4 BIT WORD
  //   7 BIT HAMMING CODE
  //   P1
  //   P2
  //   D3
  //   P4
  //   D5
  //   D6
  //   D7
  //   ERROR GENERATING CIRCUIT
  //   p1
  //   p2
  //   d3
  //   p4
  //   d5
  //   d6
  //   d7
  //   C1
  //   C2
  //   C3
  //   ERROR CORRECTION CIRCUIT
  //   c2
  //   3:8 DECODER
  //   c3
  //   c1
  //   DECODED HAMMING CODE
  //   CORRECTED INPUT CODE
  //   (DECODED CORRECTED DATA)
endmodule

module _3_8_decoder (
  input  in_1,
  input  in_2,
  input  in_3,
  output out_4,
  output out_5,
  output out_6,
  output out_7,
  output out_8,
  output out_9,
  output out_10,
  output out_11
);

  wire not_1_out, not_2_out, not_3_out, not_4_out, not_5_out, not_6_out, not_7_out, not_8_out, not_9_out,
       not_10_out, not_11_out, not_12_out;

  not not_1 (not_1_out, in_1);
  not not_2 (not_2_out, in_2);
  not not_3 (not_3_out, in_3);
  not not_4 (not_4_out, in_1);
  not not_5 (not_5_out, in_2);
  not not_6 (not_6_out, in_1);
  not not_7 (not_7_out, in_3);
  not not_8 (not_8_out, in_1);
  not not_9 (not_9_out, in_2);
  not not_10 (not_10_out, in_3);
  not not_11 (not_11_out, in_2);
  not not_12 (not_12_out, in_3);
  and and_1 (out_4, not_1_out, not_2_out, not_3_out);
  and and_2 (out_5, not_4_out, not_5_out, in_3);
  and and_3 (out_6, not_6_out, in_2, not_7_out);
  and and_4 (out_7, not_8_out, in_2, in_3);
  and and_5 (out_8, in_1, not_9_out, not_10_out);
  and and_6 (out_9, in_1, not_11_out, in_3);
  and and_7 (out_10, in_1, in_2, not_12_out);
  and and_8 (out_11, in_3, in_2, in_1);
endmodule
